# Fritzing sketch Ver.1 (saved by Fritzing 0.9.3b)

parts:
  Raspberry_Pi_1 = Raspberry Pi 3 [part_number=RPI-3-V1.2]
  M1 = RioRand LM2596
  S2 = Round Pushbutton
  U1 = TRANSCHIPTC5747 [package=camera_sfv24r-2st_2]  # not connected
  ZS-042_RTC1 = ZS-042 RTC Module
  R2 = Resistor [tolerance=±5% resistance=10k package="0402 [SMD]"]
  R4 = Resistor [tolerance=±5% resistance=10k package="0402 [SMD]"]
  S3 = Round Pushbutton
  LED1 = LEDs [package=led10mm]
  LED2 = LEDs [package=led10mm]
  LED3 = LEDs [package=led10mm]
  LED4 = LEDs [package=led10mm]
  LED5 = LEDs [package=led10mm]
  R5 = Resistor [tolerance=±5% resistance=330 package="0402 [SMD]"]
  R6 = Resistor [tolerance=±5% resistance=330 package="0402 [SMD]"]
  R7 = Resistor [tolerance=±5% resistance=330 package="0402 [SMD]"]
  R8 = Resistor [tolerance=±5% resistance=330 package="0402 [SMD]"]
  R9 = Resistor [tolerance=±5% resistance=330 package="0402 [SMD]"]
  R10 = Resistor [tolerance=±5% resistance=10k package="0402 [SMD]"]
  R11 = Resistor [tolerance=±5% resistance=330 package="0402 [SMD]"]
  R12 = Resistor [tolerance=±5% resistance=10k package="0402 [SMD]"]
  R13 = Resistor [tolerance=±5% resistance=330 package="0402 [SMD]"]

nets:
  3V3: Raspberry_Pi_1.3v3, ZS-042_RTC1.VCC, R11.Pin_1
  N1: Raspberry_Pi_1.GPIO2, ZS-042_RTC1.SDA
  N2: Raspberry_Pi_1.GPIO3, ZS-042_RTC1.SCL
  N3: Raspberry_Pi_1.GPIO5, LED5.A
  N4: Raspberry_Pi_1.GPIO6, LED4.A
  N5: Raspberry_Pi_1.GPIO13, LED3.A
  N6: Raspberry_Pi_1.GPIO19, LED2.A
  N7: Raspberry_Pi_1.GPIO26, LED1.A
  N8: Raspberry_Pi_1.GND, M1.Pin_4, R5.Pin_1, R6.Pin_1, R7.Pin_1, R8.Pin_1, R9.Pin_1
  N9: Raspberry_Pi_1.GPIO14, R2.Pin_0
  N10: S2.leg0, R10.Pin_0
  N11: S2.leg1, R11.Pin_0
  N12: R2.Pin_1, R4.Pin_0
  N13: S3.leg0, R12.Pin_0
  N14: S3.leg1, R13.Pin_0
  N15: LED1.C, R5.Pin_0
  N16: LED2.C, R6.Pin_0
  N17: LED3.C, R7.Pin_0
  N18: LED4.C, R8.Pin_0
  N19: LED5.C, R9.Pin_0

notes:
  Alarm Release Button
  5v
  SIM800l Module + Micro SimCard
  Alarm Output
  RTC Module
  PiCamera Rev.2
  LM2596 Module Set to 3.9v ~ 4.1v
  Raspberry Pi 3 B+
  Set Default Settings
  SIM800 Module
  Internet Access
  Local Network
  Local SQL Server
  Frame Toggles
  Pre-Alarm Output
  vcc
  rst
  rxd
  txd
  gnd
